// Logisim project CRC mod by Giul.circ as structural Verilog: 3 circuits, main circuit main
module main (
);

  wire clock_1_out, crc_cell_1_to_next_cell, crc_cell_2_to_next_cell, crc_cell_3_to_next_cell,
       crc_cell_4_to_next_cell, crc_cell_5_to_next_cell, crc_cell_6_to_next_cell, crc_cell_7_to_next_cell,
       crc_cell_8_to_next_cell, crc_cell_9_to_next_cell, shift_register_1_out, shift_register_2_q0,
       shift_register_2_q1, shift_register_2_q2, shift_register_2_q3, shift_register_2_q4,
       shift_register_2_q5, shift_register_2_q6, shift_register_2_q7;
  wire [3:0] crc_cell_2_output, crc_cell_7_output;

  Clock clock_1 (.out(clock_1_out));
  Shift_Register shift_register_1 (
    .in(1'b0), .clk(clock_1_out), .out(shift_register_1_out));  // open: shift, load, clr, d0, q0, d1, q1, d2, q2, d3, q3, d4, q4, d5, q5, d6, q6, d7, q7
  CRC_cell crc_cell_1 (
    .Clock(clock_1_out), .Input(shift_register_1_out), .Loopback(crc_cell_9_to_next_cell),
    .enable(shift_register_2_q0), .to_next_cell(crc_cell_1_to_next_cell));  // open: output
  Shift_Register #(.length(9)) shift_register_2 (
    .q0(shift_register_2_q0), .q1(shift_register_2_q1), .q2(shift_register_2_q2), .q3(shift_register_2_q3),
    .q4(shift_register_2_q4), .q5(shift_register_2_q5), .q6(shift_register_2_q6), .q7(shift_register_2_q7));  // open: shift, in, clk, out, load, clr, d0, d1, d2, d3, d4, d5, d6, d7, d8, q8
  CRC_cell crc_cell_2 (
    .Clock(clock_1_out), .Input(crc_cell_1_to_next_cell), .Loopback(crc_cell_9_to_next_cell),
    .enable(shift_register_2_q1), .to_next_cell(crc_cell_2_to_next_cell), .\output (crc_cell_2_output[0]));
  CRC_cell crc_cell_3 (
    .Clock(clock_1_out), .Input(crc_cell_2_to_next_cell), .Loopback(crc_cell_9_to_next_cell),
    .enable(shift_register_2_q2), .to_next_cell(crc_cell_3_to_next_cell), .\output (crc_cell_2_output[1]));
  CRC_cell crc_cell_4 (
    .Clock(clock_1_out), .Input(crc_cell_3_to_next_cell), .Loopback(crc_cell_9_to_next_cell),
    .enable(shift_register_2_q3), .to_next_cell(crc_cell_4_to_next_cell), .\output (crc_cell_2_output[2]));
  CRC_cell crc_cell_5 (
    .Clock(clock_1_out), .Input(crc_cell_4_to_next_cell), .Loopback(crc_cell_9_to_next_cell),
    .enable(shift_register_2_q4), .to_next_cell(crc_cell_5_to_next_cell), .\output (crc_cell_2_output[3]));
  CRC_cell crc_cell_6 (
    .Clock(clock_1_out), .Input(crc_cell_7_to_next_cell), .Loopback(crc_cell_9_to_next_cell),
    .enable(shift_register_2_q6), .to_next_cell(crc_cell_6_to_next_cell), .\output (crc_cell_7_output[1]));
  CRC_cell crc_cell_7 (
    .Clock(clock_1_out), .Input(crc_cell_5_to_next_cell), .Loopback(crc_cell_9_to_next_cell),
    .enable(shift_register_2_q5), .to_next_cell(crc_cell_7_to_next_cell), .\output (crc_cell_7_output[0]));
  Hex_Digit_Display hex_digit_display_1 (.value(crc_cell_2_output));  // open: dp
  Hex_Digit_Display hex_digit_display_2 (.value(crc_cell_7_output));  // open: dp
  CRC_cell crc_cell_8 (
    .Clock(clock_1_out), .Input(crc_cell_6_to_next_cell), .Loopback(crc_cell_9_to_next_cell),
    .enable(shift_register_2_q7), .to_next_cell(crc_cell_8_to_next_cell), .\output (crc_cell_7_output[2]));
  CRC_cell crc_cell_9 (
    .Clock(clock_1_out), .Input(crc_cell_8_to_next_cell), .Loopback(crc_cell_9_to_next_cell), .enable(1'b0),
    .to_next_cell(crc_cell_9_to_next_cell), .\output (crc_cell_7_output[3]));

  // Notes on the sheet:
  //   Il circuito riceve MSB prima
  //   LSB
  //   MSB
  //   Polynomial: LSB on the left, MSB on the right
  //   Note: MSB is NEVER enabled!
endmodule

module CRC_cell (
  input  Clock,
  input  Input,
  input  Loopback,
  input  enable,
  output \output ,
  output to_next_cell
);

  wire and_1_out;

  D_Flip_Flop d_ff_1 (.clk(Clock), .D(Input), .Q(\output ));  // open: Qn, preset, en, reset
  and and_1 (and_1_out, Loopback, enable);
  xor xor_1 (to_next_cell, \output , and_1_out);

  // Notes on the sheet:
  //   Basic CRC element. Loopback comes from the last FLIP-FLOP output
endmodule

module CRC_Cell_Giul (
  input  Clock,
  input  Input,
  input  Loopback,
  input  enable,
  output to_next_cell
);

  wire and_1_out, xor_1_out;

  and and_1 (and_1_out, Loopback, enable);
  xor xor_1 (xor_1_out, Input, and_1_out);
  D_Flip_Flop d_ff_1 (.clk(Clock), .D(xor_1_out), .Q(to_next_cell));  // open: Qn, preset, en, reset

  // Notes on the sheet:
  //   Basic CRC element. Loopback comes from the last FLIP-FLOP output
endmodule
