// Logisim project CRC.circ as structural Verilog: 2 circuits, main circuit main
module main (
);

  wire clock_1_out, crc_cell_1_output, shift_register_1_out, shift_register_2_q0, shift_register_2_q1,
       shift_register_2_q2, shift_register_2_q3, shift_register_2_q4, shift_register_2_q5,
       shift_register_2_q6, shift_register_2_q7;
  wire [3:0] crc_cell_2_output, crc_cell_7_output;

  Clock clock_1 (.out(clock_1_out));
  Shift_Register shift_register_1 (
    .in(1'b0), .clk(clock_1_out), .out(shift_register_1_out));  // open: shift, load, clr, d0, q0, d1, q1, d2, q2, d3, q3, d4, q4, d5, q5, d6, q6, d7, q7
  CRC_cell crc_cell_1 (
    .Clock(clock_1_out), .Input(shift_register_1_out), .Loopback(crc_cell_7_output[3]),
    .enable(shift_register_2_q0), .Output(crc_cell_1_output));
  Shift_Register #(.length(9)) shift_register_2 (
    .q0(shift_register_2_q0), .q1(shift_register_2_q1), .q2(shift_register_2_q2), .q3(shift_register_2_q3),
    .q4(shift_register_2_q4), .q5(shift_register_2_q5), .q6(shift_register_2_q6), .q7(shift_register_2_q7));  // open: shift, in, clk, out, load, clr, d0, d1, d2, d3, d4, d5, d6, d7, d8, q8
  CRC_cell crc_cell_2 (
    .Clock(clock_1_out), .Input(crc_cell_1_output), .Loopback(crc_cell_7_output[3]),
    .enable(shift_register_2_q1), .Output(crc_cell_2_output[0]));
  CRC_cell crc_cell_3 (
    .Clock(clock_1_out), .Input(crc_cell_2_output[0]), .Loopback(crc_cell_7_output[3]),
    .enable(shift_register_2_q2), .Output(crc_cell_2_output[1]));
  CRC_cell crc_cell_4 (
    .Clock(clock_1_out), .Input(crc_cell_2_output[1]), .Loopback(crc_cell_7_output[3]),
    .enable(shift_register_2_q3), .Output(crc_cell_2_output[2]));
  CRC_cell crc_cell_5 (
    .Clock(clock_1_out), .Input(crc_cell_2_output[2]), .Loopback(crc_cell_7_output[3]),
    .enable(shift_register_2_q4), .Output(crc_cell_2_output[3]));
  CRC_cell crc_cell_6 (
    .Clock(clock_1_out), .Input(crc_cell_7_output[0]), .Loopback(crc_cell_7_output[3]),
    .enable(shift_register_2_q6), .Output(crc_cell_7_output[1]));
  CRC_cell crc_cell_7 (
    .Clock(clock_1_out), .Input(crc_cell_2_output[3]), .Loopback(crc_cell_7_output[3]),
    .enable(shift_register_2_q5), .Output(crc_cell_7_output[0]));
  Hex_Digit_Display hex_digit_display_1 (.value(crc_cell_2_output));  // open: dp
  Hex_Digit_Display hex_digit_display_2 (.value(crc_cell_7_output));  // open: dp
  CRC_cell crc_cell_8 (
    .Clock(clock_1_out), .Input(crc_cell_7_output[1]), .Loopback(crc_cell_7_output[3]),
    .enable(shift_register_2_q7), .Output(crc_cell_7_output[2]));
  CRC_cell crc_cell_9 (
    .Clock(clock_1_out), .Input(crc_cell_7_output[2]), .Loopback(crc_cell_7_output[3]), .enable(1'b0),
    .Output(crc_cell_7_output[3]));

  // Notes on the sheet:
  //   Il circuito riceve MSB prima
  //   LSB
  //   MSB
  //   Polynomial: LSB on the left, MSB on the right
  //   Note: MSB is NEVER enabled!
endmodule

module CRC_cell (
  input  Clock,
  input  Input,
  input  Loopback,
  input  enable,
  output Output
);

  wire and_1_out, d_ff_1_q;

  D_Flip_Flop d_ff_1 (.clk(Clock), .D(Input), .Q(d_ff_1_q));  // open: Qn, preset, en, reset
  and and_1 (and_1_out, Loopback, enable);
  xor xor_1 (Output, d_ff_1_q, and_1_out);

  // Notes on the sheet:
  //   Basic CRC element. Loopback comes from the last FLIP-FLOP output
  //   No. Non è così. Lo XOR va alla cella successiva, il Q diventa il CRC
endmodule
