// Logisim project CRC_Logic_basic.circ as structural Verilog: 2 circuits, main circuit main
module main (
  input  CLK,
  input  INPUT,
  input  OUTPUT,
  input  IN_XOR,
  input  XOR_ENABLE,
  input  RESET
);

  wire do_xor_1_c;

  do_xor do_xor_1 (.B(INPUT), .A(IN_XOR), .C(do_xor_1_c), .Enable(XOR_ENABLE));
  D_Flip_Flop d_ff_1 (.clk(CLK), .D(do_xor_1_c), .Q(OUTPUT), .reset(RESET));  // open: Qn, preset, en
endmodule

module do_xor (
  input  B,
  input  A,
  input  Enable,
  output C
);

  wire and_1_out;

  and and_1 (and_1_out, A, Enable);
  xor xor_1 (C, B, and_1_out);
endmodule
