// Logisim project CRC_Module_all.circ as structural Verilog: 5 circuits, main circuit ModuloCRCALL
module ModuloCRCALL (
  input  MD__selects_the_behaviour_of_the_chip,
  input  Line_IN,
  input  Clock,
  input  Reset,
  output Line_out,
  output Busy
);

  wire CRC_Control_u, CRC_Logic_p3, MD_Enable_output, Shift_Register_out;

  MD_Enable MD_Enable (
    .in_a(MD__selects_the_behaviour_of_the_chip), .in_b(Busy), .in_c(Line_IN), .\output (MD_Enable_output),
    .in_d(CRC_Control_u));
  Shift_Register Shift_Register (
    .in(MD_Enable_output), .out(Shift_Register_out));  // open: shift, clk, load, clr, d0, q0, d1, q1, d2, q2, d3, q3, d4, q4, d5, q5, d6, q6, d7, q7
  CRC_Controller CRC_Control (.Q(Busy), .U(CRC_Control_u));  // open: Clock, Reset
  // CRC_Logic CRC_Logic: pin names not known; wires that end beside it: MD_Enable_output, CRC_Control_u, CRC_Logic_p3
  Multiplexer #(.enable("false")) multiplexer_1 (
    .in0(Shift_Register_out), .in1(CRC_Logic_p3), .out(Line_out), .sel(Busy));

  // Notes on the sheet:
  //   Connected to clock lines
  //   Connected to reset lines
  //   crc_enable
  //   crc_control_out
endmodule

// do_xor
module Do_XOR (
  input  B,
  input  A,
  input  E,
  output C
);

  wire and_1_out;

  and and_1 (and_1_out, A, E);
  xor xor_1 (C, B, and_1_out);
endmodule

module MD_Enable (
  input  in_a,
  input  in_d,
  input  in_b,
  input  in_c,
  output \output 
);

  wire and_1_out, not_1_out, or_1_out;

  and and_1 (and_1_out, in_a, in_d);
  not not_1 (not_1_out, in_b);
  or or_1 (or_1_out, and_1_out, not_1_out);
  and and_2 (\output , or_1_out, in_c);
endmodule

module CRC_Logic (
  input  Reset,
  input  Clock,
  input  D,
  input  Enable,
  output Q
);

  wire d_ff_1_q, d_ff_2_q, d_ff_3_q, d_ff_4_q, d_ff_5_q, d_ff_6_q, d_ff_7_q, undriven, x_0_c, x_2_c, x_4_c;

  Do_XOR x_0 (.B(D), .A(Q), .E(Enable), .C(x_0_c));
  D_Flip_Flop d_ff_1 (.clk(Clock), .D(x_0_c), .Q(d_ff_1_q));  // open: Qn, preset, en, reset
  D_Flip_Flop d_ff_2 (.clk(Clock), .D(d_ff_1_q), .Q(d_ff_2_q));  // open: Qn, preset, en, reset
  D_Flip_Flop d_ff_3 (
    .clk(Clock), .D(x_2_c), .Q(d_ff_3_q), .preset(undriven), .en(undriven), .reset(undriven));  // open: Qn
  Do_XOR x_2 (.B(d_ff_2_q), .A(Q), .E(Enable), .C(x_2_c));
  D_Flip_Flop d_ff_4 (.clk(Clock), .D(d_ff_3_q), .Q(d_ff_4_q));  // open: Qn, preset, en, reset
  Do_XOR x_4 (.B(d_ff_4_q), .A(Q), .E(Enable), .C(x_4_c));
  D_Flip_Flop d_ff_5 (.clk(Clock), .D(x_4_c), .Q(d_ff_5_q));  // open: Qn, preset, en, reset
  D_Flip_Flop d_ff_6 (.clk(Clock), .D(d_ff_5_q), .Q(d_ff_6_q));  // open: Qn, preset, en, reset
  D_Flip_Flop d_ff_7 (.clk(Clock), .D(d_ff_6_q), .Q(d_ff_7_q));  // open: Qn, preset, en, reset
  D_Flip_Flop d_ff_8 (.clk(Clock), .D(d_ff_7_q), .Q(Q));  // open: Qn, preset, en, reset

  // Notes on the sheet:
  //   Connected to FF reset lines
endmodule

module CRC_Controller (
  input  Clock,
  input  Reset,
  output Q,
  output U
);
endmodule
