// Logisim project crc_SR+XOR.circ as structural Verilog: 1 circuit, main circuit main
module main (
);

  wire clock_1_out, d_ff_1_q, shift_register_1_out, xor_1_out, xor_2_out, xor_3_out;
  wire [3:0] d_ff_2_q, d_ff_6_q;

  Clock clock_1 (.out(clock_1_out));
  D_Flip_Flop d_ff_1 (.clk(clock_1_out), .D(shift_register_1_out), .Q(d_ff_1_q));  // open: Qn, preset, en, reset
  D_Flip_Flop d_ff_2 (.clk(clock_1_out), .D(xor_1_out), .Q(d_ff_2_q[0]));  // open: Qn, preset, en, reset
  xor xor_1 (xor_1_out, d_ff_1_q, d_ff_6_q[3]);
  Shift_Register shift_register_1 (
    .in(1'b0), .clk(clock_1_out), .out(shift_register_1_out));  // open: shift, load, clr, d0, q0, d1, q1, d2, q2, d3, q3, d4, q4, d5, q5, d6, q6, d7, q7
  D_Flip_Flop d_ff_3 (.clk(clock_1_out), .D(xor_2_out), .Q(d_ff_2_q[1]));  // open: Qn, preset, en, reset
  xor xor_2 (xor_2_out, d_ff_2_q[0], d_ff_6_q[3]);
  Hex_Digit_Display hex_digit_display_1 (.value(d_ff_6_q));  // open: dp
  D_Flip_Flop d_ff_4 (.clk(clock_1_out), .D(xor_3_out), .Q(d_ff_2_q[2]));  // open: Qn, preset, en, reset
  xor xor_3 (xor_3_out, d_ff_2_q[1], d_ff_6_q[3]);
  Hex_Digit_Display hex_digit_display_2 (.value(d_ff_2_q));  // open: dp
  D_Flip_Flop d_ff_5 (.clk(clock_1_out), .D(d_ff_2_q[2]), .Q(d_ff_2_q[3]));  // open: Qn, preset, en, reset
  D_Flip_Flop d_ff_6 (.clk(clock_1_out), .D(d_ff_2_q[3]), .Q(d_ff_6_q[0]));  // open: Qn, preset, en, reset
  D_Flip_Flop d_ff_7 (.clk(clock_1_out), .D(d_ff_6_q[0]), .Q(d_ff_6_q[1]));  // open: Qn, preset, en, reset
  D_Flip_Flop d_ff_8 (.clk(clock_1_out), .D(d_ff_6_q[1]), .Q(d_ff_6_q[2]));  // open: Qn, preset, en, reset
  D_Flip_Flop d_ff_9 (.clk(clock_1_out), .D(d_ff_6_q[2]), .Q(d_ff_6_q[3]));  // open: Qn, preset, en, reset

  // Notes on the sheet:
  //   Wikipedia example.
  //   Message: "W" - 01010111
  //   CRC: 0xA2
  //   CRC Polynomial = x^8+x^2+x+1
  //   The shift register feeds the CRC Logic, then the result comes after nine bits of zero
endmodule
